// Digital circuit ex.dig as structural Verilog
module ex (
  input  [7:0] aluop__i,
  input  [2:0] alusel__i,
  input  [31:0] reg1__i,
  input  [31:0] reg2__i,
  input  [4:0] wd__i,
  input  wreg__i,
  input  rst,
  output [31:0] wdata__o,
  output [4:0] wd__o,
  output wreg__o
);

  wire [31:0] logic_alu_1_a;

  logic_alu logic_alu_1 (.reg1(reg1__i), .reg2(reg2__i), .aluop(aluop__i), .rst(rst), .A(logic_alu_1_a));
  Multiplexer #(.Bits(32), .Selector_Bits(3)) multiplexer_1 (
    .sel(alusel__i), .in_0({32{1'b0}}), .in_1(logic_alu_1_a), .in_2({32{1'b0}}), .in_3({32{1'b0}}),
    .in_4({32{1'b0}}), .in_5({32{1'b0}}), .in_6({32{1'b0}}), .in_7({32{1'b0}}), .out(wdata__o));

  assign wd__o = wd__i;
  assign wreg__o = wreg__i;

  // Notes on the sheet:
  //   aluop__i: 執行階段要進行的運算的子類型
  //   alusel__i: 執行階段要進行的運算的類型
  //   reg1__i: 參與運算的來源操作數1
  //   reg2__i: 參與運算的來源操作數2
  //   wd__i: 指令執行要寫入的目的暫存器位址
  //   wreg__i: 是否有要寫入的目的暫存器
  //   rst: 復位訊號
  //   wdata__o: 執行階段的指令最終要寫入目的暫存器的值
  //   wd__o: 執行階段的指令最終要寫入的目的暫存器位址
  //   wreg__o: 執行階段的指令最終是否有要寫入的目的暫存器
endmodule
