// Digital circuit logic_alu.dig as structural Verilog
module logic_alu (
  input  [31:0] reg1,
  input  [31:0] reg2,
  input  [7:0] aluop,
  input  rst,
  output [31:0] A
);

  wire [31:0] multiplexer_1_out, or_1_out;

  assign or_1_out = reg1 | reg2;  // Or or_1, 32 bits wide
  Multiplexer #(.Selector_Bits(8), .Bits(32)) multiplexer_1 (
    .sel(aluop), .in_0({32{1'b0}}), .in_1({32{1'b0}}), .in_2({32{1'b0}}), .in_3({32{1'b0}}),
    .in_4({32{1'b0}}), .in_5({32{1'b0}}), .in_6({32{1'b0}}), .in_7({32{1'b0}}), .in_8({32{1'b0}}),
    .in_9({32{1'b0}}), .in_10({32{1'b0}}), .in_11({32{1'b0}}), .in_12({32{1'b0}}), .in_13({32{1'b0}}),
    .in_14({32{1'b0}}), .in_15({32{1'b0}}), .in_16({32{1'b0}}), .in_17({32{1'b0}}), .in_18({32{1'b0}}),
    .in_19({32{1'b0}}), .in_20({32{1'b0}}), .in_21({32{1'b0}}), .in_22({32{1'b0}}), .in_23({32{1'b0}}),
    .in_24({32{1'b0}}), .in_25({32{1'b0}}), .in_26({32{1'b0}}), .in_27({32{1'b0}}), .in_28({32{1'b0}}),
    .in_29({32{1'b0}}), .in_30({32{1'b0}}), .in_31({32{1'b0}}), .in_32({32{1'b0}}), .in_33({32{1'b0}}),
    .in_34({32{1'b0}}), .in_35({32{1'b0}}), .in_36({32{1'b0}}), .in_37(or_1_out), .in_38({32{1'b0}}),
    .in_39({32{1'b0}}), .in_40({32{1'b0}}), .in_41({32{1'b0}}), .in_42({32{1'b0}}), .in_43({32{1'b0}}),
    .in_44({32{1'b0}}), .in_45({32{1'b0}}), .in_46({32{1'b0}}), .in_47({32{1'b0}}), .in_48({32{1'b0}}),
    .in_49({32{1'b0}}), .in_50({32{1'b0}}), .in_51({32{1'b0}}), .in_52({32{1'b0}}), .in_53({32{1'b0}}),
    .in_54({32{1'b0}}), .in_55({32{1'b0}}), .in_56({32{1'b0}}), .in_57({32{1'b0}}), .in_58({32{1'b0}}),
    .in_59({32{1'b0}}), .in_60({32{1'b0}}), .in_61({32{1'b0}}), .in_62({32{1'b0}}), .in_63({32{1'b0}}),
    .in_64({32{1'b0}}), .in_65({32{1'b0}}), .in_66({32{1'b0}}), .in_67({32{1'b0}}), .in_68({32{1'b0}}),
    .in_69({32{1'b0}}), .in_70({32{1'b0}}), .in_71({32{1'b0}}), .in_72({32{1'b0}}), .in_73({32{1'b0}}),
    .in_74({32{1'b0}}), .in_75({32{1'b0}}), .in_76({32{1'b0}}), .in_77({32{1'b0}}), .in_78({32{1'b0}}),
    .in_79({32{1'b0}}), .in_80({32{1'b0}}), .in_81({32{1'b0}}), .in_82({32{1'b0}}), .in_83({32{1'b0}}),
    .in_84({32{1'b0}}), .in_85({32{1'b0}}), .in_86({32{1'b0}}), .in_87({32{1'b0}}), .in_88({32{1'b0}}),
    .in_89({32{1'b0}}), .in_90({32{1'b0}}), .in_91({32{1'b0}}), .in_92({32{1'b0}}), .in_93({32{1'b0}}),
    .in_94({32{1'b0}}), .in_95({32{1'b0}}), .in_96({32{1'b0}}), .in_97({32{1'b0}}), .in_98({32{1'b0}}),
    .in_99({32{1'b0}}), .in_100({32{1'b0}}), .in_101({32{1'b0}}), .in_102({32{1'b0}}), .in_103({32{1'b0}}),
    .in_104({32{1'b0}}), .in_105({32{1'b0}}), .in_106({32{1'b0}}), .in_107({32{1'b0}}), .in_108({32{1'b0}}),
    .in_109({32{1'b0}}), .in_110({32{1'b0}}), .in_111({32{1'b0}}), .in_112({32{1'b0}}), .in_113({32{1'b0}}),
    .in_114({32{1'b0}}), .in_115({32{1'b0}}), .in_116({32{1'b0}}), .in_117({32{1'b0}}), .in_118({32{1'b0}}),
    .in_119({32{1'b0}}), .in_120({32{1'b0}}), .in_121({32{1'b0}}), .in_122({32{1'b0}}), .in_123({32{1'b0}}),
    .in_124({32{1'b0}}), .in_125({32{1'b0}}), .in_126({32{1'b0}}), .in_127({32{1'b0}}), .in_128({32{1'b0}}),
    .in_129({32{1'b0}}), .in_130({32{1'b0}}), .in_131({32{1'b0}}), .in_132({32{1'b0}}), .in_133({32{1'b0}}),
    .in_134({32{1'b0}}), .in_135({32{1'b0}}), .in_136({32{1'b0}}), .in_137({32{1'b0}}), .in_138({32{1'b0}}),
    .in_139({32{1'b0}}), .in_140({32{1'b0}}), .in_141({32{1'b0}}), .in_142({32{1'b0}}), .in_143({32{1'b0}}),
    .in_144({32{1'b0}}), .in_145({32{1'b0}}), .in_146({32{1'b0}}), .in_147({32{1'b0}}), .in_148({32{1'b0}}),
    .in_149({32{1'b0}}), .in_150({32{1'b0}}), .in_151({32{1'b0}}), .in_152({32{1'b0}}), .in_153({32{1'b0}}),
    .in_154({32{1'b0}}), .in_155({32{1'b0}}), .in_156({32{1'b0}}), .in_157({32{1'b0}}), .in_158({32{1'b0}}),
    .in_159({32{1'b0}}), .in_160({32{1'b0}}), .in_161({32{1'b0}}), .in_162({32{1'b0}}), .in_163({32{1'b0}}),
    .in_164({32{1'b0}}), .in_165({32{1'b0}}), .in_166({32{1'b0}}), .in_167({32{1'b0}}), .in_168({32{1'b0}}),
    .in_169({32{1'b0}}), .in_170({32{1'b0}}), .in_171({32{1'b0}}), .in_172({32{1'b0}}), .in_173({32{1'b0}}),
    .in_174({32{1'b0}}), .in_175({32{1'b0}}), .in_176({32{1'b0}}), .in_177({32{1'b0}}), .in_178({32{1'b0}}),
    .in_179({32{1'b0}}), .in_180({32{1'b0}}), .in_181({32{1'b0}}), .in_182({32{1'b0}}), .in_183({32{1'b0}}),
    .in_184({32{1'b0}}), .in_185({32{1'b0}}), .in_186({32{1'b0}}), .in_187({32{1'b0}}), .in_188({32{1'b0}}),
    .in_189({32{1'b0}}), .in_190({32{1'b0}}), .in_191({32{1'b0}}), .in_192({32{1'b0}}), .in_193({32{1'b0}}),
    .in_194({32{1'b0}}), .in_195({32{1'b0}}), .in_196({32{1'b0}}), .in_197({32{1'b0}}), .in_198({32{1'b0}}),
    .in_199({32{1'b0}}), .in_200({32{1'b0}}), .in_201({32{1'b0}}), .in_202({32{1'b0}}), .in_203({32{1'b0}}),
    .in_204({32{1'b0}}), .in_205({32{1'b0}}), .in_206({32{1'b0}}), .in_207({32{1'b0}}), .in_208({32{1'b0}}),
    .in_209({32{1'b0}}), .in_210({32{1'b0}}), .in_211({32{1'b0}}), .in_212({32{1'b0}}), .in_213({32{1'b0}}),
    .in_214({32{1'b0}}), .in_215({32{1'b0}}), .in_216({32{1'b0}}), .in_217({32{1'b0}}), .in_218({32{1'b0}}),
    .in_219({32{1'b0}}), .in_220({32{1'b0}}), .in_221({32{1'b0}}), .in_222({32{1'b0}}), .in_223({32{1'b0}}),
    .in_224({32{1'b0}}), .in_225({32{1'b0}}), .in_226({32{1'b0}}), .in_227({32{1'b0}}), .in_228({32{1'b0}}),
    .in_229({32{1'b0}}), .in_230({32{1'b0}}), .in_231({32{1'b0}}), .in_232({32{1'b0}}), .in_233({32{1'b0}}),
    .in_234({32{1'b0}}), .in_235({32{1'b0}}), .in_236({32{1'b0}}), .in_237({32{1'b0}}), .in_238({32{1'b0}}),
    .in_239({32{1'b0}}), .in_240({32{1'b0}}), .in_241({32{1'b0}}), .in_242({32{1'b0}}), .in_243({32{1'b0}}),
    .in_244({32{1'b0}}), .in_245({32{1'b0}}), .in_246({32{1'b0}}), .in_247({32{1'b0}}), .in_248({32{1'b0}}),
    .in_249({32{1'b0}}), .in_250({32{1'b0}}), .in_251({32{1'b0}}), .in_252({32{1'b0}}), .in_253({32{1'b0}}),
    .in_254({32{1'b0}}), .in_255({32{1'b0}}), .out(multiplexer_1_out));
  Multiplexer #(.Bits(32)) multiplexer_2 (.sel(rst), .in_0(multiplexer_1_out), .in_1({32{1'b0}}), .out(A));
endmodule
