// Digital circuit ex_mem.dig as structural Verilog
module ex_mem (
  input  [31:0] ex__wdata,
  input  [4:0] ex__wd,
  input  ex__wreg,
  input  rst,
  input  clk,
  output [31:0] mem__wdata,
  output [4:0] mem__wd,
  output mem__wreg
);

  wire multiplexer_2_out;
  wire [4:0] multiplexer_1_out;
  wire [31:0] multiplexer_3_out;

  Multiplexer #(.Bits(5)) multiplexer_1 (.sel(rst), .in_0(ex__wd), .in_1({5{1'b0}}), .out(multiplexer_1_out));
  Multiplexer multiplexer_2 (.sel(rst), .in_0(ex__wreg), .in_1(1'b0), .out(multiplexer_2_out));
  Multiplexer #(.Bits(32)) multiplexer_3 (.sel(rst), .in_0(ex__wdata), .in_1({32{1'b0}}), .out(multiplexer_3_out));
  Register #(.Bits(5)) register_1 (.D(multiplexer_1_out), .C(clk), .en(1'b1), .Q(mem__wd));
  Register register_2 (.D(multiplexer_2_out), .C(clk), .en(1'b1), .Q(mem__wreg));
  Register #(.Bits(32)) register_3 (.D(multiplexer_3_out), .C(clk), .en(1'b1), .Q(mem__wdata));

  // Notes on the sheet:
  //   ex__wdata: 執行階段的指令要寫入目的暫存器的值
  //   ex__wd: 執行階段的指令執行後要寫入的目的暫存器位址
  //   ex__wreg: 執行階段的指令執行後是否有要寫入的目的暫存器
  //   rst: 復位訊號
  //   mem__wdata: 訪存階段的指令要寫入目的暫存器的值
  //   mem__wd: 訪存階段的指令執行後要寫入的目的暫存器位址
  //   mem__wreg: 訪存階段的指令執行後是否有要寫入的目的暫存器
endmodule
