// Digital circuit addr_control.dig as structural Verilog
module addr_control (
  input  [4:0] addr_i,
  input  en,
  input  rst,
  output [4:0] addr_o
);

  wire [4:0] multiplexer_1_out;

  Multiplexer #(.Bits(5)) multiplexer_1 (.sel(en), .in_0({5{1'b0}}), .in_1(addr_i), .out(multiplexer_1_out));
  Multiplexer #(.Bits(5)) multiplexer_2 (.sel(rst), .in_0(multiplexer_1_out), .in_1({5{1'b0}}), .out(addr_o));
endmodule
