// Digital circuit decoder.dig as structural Verilog
module decoder (
  input  [5:0] op,
  input  [5:0] func,
  output [7:0] aluop,
  output [2:0] alusel,
  output reg1__read,
  output reg2__read,
  output imm__read,
  output shamt__read,
  output addr__read,
  output wreg
);

  wire comparator_1_eq;
  wire [14:0] multiplexer_1_out;
  wire [31:0] func_out, op_out;

  LookUpTable #(.Bits(32)) u_op (
    .in0(op[0]), .in1(op[1]), .in2(op[2]), .in3(op[3]), .in4(op[4]), .in5(op[5]), .out(op_out));
  LookUpTable #(.Bits(32)) u_func (
    .in0(func[0]), .in1(func[1]), .in2(func[2]), .in3(func[3]), .in4(func[4]), .in5(func[5]), .out(func_out));
  Comparator #(.Bits(6)) comparator_1 (.a(op), .b({6{1'b0}}), .eq(comparator_1_eq));  // open: gt, lt
  Multiplexer #(.Bits(32)) multiplexer_1 (
    .sel(comparator_1_eq), .in_0(op_out), .in_1(func_out),
    .out({alusel, aluop, reg1__read, reg2__read, imm__read, shamt__read, addr__read, wreg, multiplexer_1_out}));

  // Notes on the sheet:
  //   aluop: 譯碼階段的指令要進行的運算的子類型
  //   alusel: 譯碼階段的指令要進行的運算的類型
  //   reg1__read: Regfile 模組的第一個讀取暫存器連接埠的讀取啟用訊號
  //   reg2__read: Regfile 模組的第二個讀取暫存器連接埠的讀取啟用訊號
  //   wreg: 譯碼階段的指令是否有要寫入的目的暫存器
  //   contents of op (hex, n*v repeats v):
  //   13*0,24b48000
  //   contents of func (hex, n*v repeats v):
  //   13*0,24b4
endmodule
