// Digital circuit id.dig as structural Verilog
module id (
  input  [31:0] pc__i,
  input  [31:0] inst__i,
  input  [31:0] reg1__data__i,
  input  [31:0] reg2__data__i,
  input  rst,
  output [7:0] aluop__o,
  output [2:0] alusel__o,
  output [4:0] wd__o,
  output wreg__o,
  output [4:0] reg2__addr__o,
  output reg2__read__o,
  output [4:0] reg1__addr__o,
  output reg1__read__o,
  output [31:0] reg1__o,
  output [31:0] reg2__o
);

  wire addr__read, imm__read, shamt__read;

  decoder decoder_1 (
    .op(inst__i[31:26]), .func(inst__i[5:0]), .aluop(aluop__o), .alusel(alusel__o),
    .reg1__read(reg1__read__o), .reg2__read(reg2__read__o), .imm__read(imm__read), .shamt__read(shamt__read),
    .addr__read(addr__read), .wreg(wreg__o));
  wd_control wd_control_1 (.rt(inst__i[20:16]), .rd(inst__i[15:11]), .imm__read(imm__read), .rst(rst), .w__addr(wd__o));
  reg_data_control reg_data_control_1 (
    .imm({{16{1'b0}}, inst__i[15:0]}), .shamt({reg1__data__i[31:5], inst__i[10:6]}),
    .reg__data_i({reg1__data__i[31:5], inst__i[10:6]}), .reg__en(reg1__read__o), .shamt__en(shamt__read),
    .rst(rst), .reg__data_o(reg1__o));
  reg_data_control reg_data_control_2 (
    .imm({{16{1'b0}}, inst__i[15:0]}), .shamt({reg1__data__i[31:5], inst__i[10:6]}),
    .reg__data_i(reg2__data__i), .reg__en(reg2__read__o), .shamt__en(shamt__read), .rst(rst),
    .reg__data_o(reg2__o));
  addr_control addr_control_1 (.addr_i(inst__i[25:21]), .en(reg1__read__o), .rst(rst), .addr_o(reg1__addr__o));
  addr_control addr_control_2 (.addr_i(inst__i[20:16]), .en(reg2__read__o), .rst(rst), .addr_o(reg2__addr__o));

  assign reg1__data__i[4:0] = inst__i[10:6];
  // also tied to GND on the sheet: {reg1__data__i[5], reg1__data__i[6], reg1__data__i[7], reg1__data__i[8], reg1__data__i[9], reg1__data__i[10], reg1__data__i[11], reg1__data__i[12], reg1__data__i[13], reg1__data__i[14], reg1__data__i[15], reg1__data__i[16], reg1__data__i[17], reg1__data__i[18], reg1__data__i[19], reg1__data__i[20], reg1__data__i[21], reg1__data__i[22], reg1__data__i[23], reg1__data__i[24], reg1__data__i[25], reg1__data__i[26], reg1__data__i[27], reg1__data__i[28], reg1__data__i[29], reg1__data__i[30], reg1__data__i[31]}

  // Other names for the same wires on the sheet: reg1__data[31:0] = {reg1__data__i[31:5], inst__i[10:6]};
  //   aluop[7:0] = aluop__o; alusel[2:0] = alusel__o; address[25:0] = inst__i[25:0]; func[5:0] = inst__i[5:0];
  //   imm[15:0] = inst__i[15:0]; shamt[4:0] = inst__i[10:6]; rd[4:0] = inst__i[15:11]; rt[4:0] = inst__i[20:16];
  //   rs[4:0] = inst__i[25:21]; op[5:0] = inst__i[31:26]; reg1__read = reg1__read__o;
  //   reg2__data[31:0] = reg2__data__i; reg2__read = reg2__read__o; wreg = wreg__o

  // Notes on the sheet:
  //   pc__i: 譯碼階段指令對應的地址
  //   inst__i: 譯碼階段的指令
  //   reg1__data__i: 從 Regfile 輸入的第一個讀取暫存器連接埠的輸入
  //   reg2__data__i: 從 Regfile 輸入的第二個讀取暫存器連接埠的輸入
  //   rst: 復位信號
  //   aluop__o: 譯碼階段的指令要進行的運算的子類型
  //   alusel__o: 譯碼階段的指令要進行的運算的類型
  //   wd__o: 譯碼階段的指令要寫入的目的暫存器位址
  //   wreg__o: 譯碼階段的指令是否有要寫入的目的暫存器
  //   reg2__addr__o: Regfile 模組的第二個讀取暫存器連接埠的讀取位址訊號
  //   reg2__read__o: Regfile 模組的第二個讀取暫存器連接埠的讀取啟用訊號
  //   reg1__addr__o: Regfile 模組的第一個讀取暫存器連接埠的讀取位址訊號
  //   reg1__read__o: Regfile 模組的第一個讀取暫存器連接埠的讀取啟用訊號
  //   reg1__o: 譯碼階段的指令要進行的運算的來源操作數1
  //   reg2__o: 譯碼階段的指令要進行的運算的來源操作數1
endmodule
