// Digital circuit reg_data_control.dig as structural Verilog
module reg_data_control (
  input  [31:0] imm,
  input  [31:0] shamt,
  input  [31:0] reg__data_i,
  input  reg__en,
  input  shamt__en,
  input  rst,
  output [31:0] reg__data_o
);

  wire [31:0] multiplexer_1_out, multiplexer_2_out;

  Multiplexer #(.Bits(32)) multiplexer_1 (.sel(shamt__en), .in_0(imm), .in_1(shamt), .out(multiplexer_1_out));
  Multiplexer #(.Bits(32)) multiplexer_2 (
    .sel(reg__en), .in_0(multiplexer_1_out), .in_1(reg__data_i), .out(multiplexer_2_out));
  Multiplexer #(.Bits(32)) multiplexer_3 (.sel(rst), .in_0(multiplexer_2_out), .in_1({32{1'b0}}), .out(reg__data_o));
endmodule
