// Digital circuit wd_control.dig as structural Verilog
module wd_control (
  input  [4:0] rt,
  input  [4:0] rd,
  input  imm__read,
  input  rst,
  output [4:0] w__addr
);

  wire [4:0] multiplexer_1_out;

  Multiplexer #(.Bits(5)) multiplexer_1 (.sel(imm__read), .in_0(rd), .in_1(rt), .out(multiplexer_1_out));
  Multiplexer #(.Bits(5)) multiplexer_2 (.sel(rst), .in_0(multiplexer_1_out), .in_1({5{1'b0}}), .out(w__addr));
endmodule
