// Digital circuit id_ex.dig as structural Verilog
module id_ex (
  input  [7:0] id__aluop,
  input  [2:0] id__alusel,
  input  [31:0] id__reg1,
  input  [31:0] id__reg2,
  input  [4:0] id__wd,
  input  id__wreg,
  input  rst,
  input  clk,
  output [7:0] ex__aluop,
  output [2:0] ex__alusel,
  output [31:0] ex__reg1,
  output [31:0] ex__reg2,
  output [4:0] ex__wd,
  output ex__wreg
);

  wire multiplexer_6_out;
  wire [2:0] multiplexer_1_out;
  wire [4:0] multiplexer_5_out;
  wire [7:0] multiplexer_2_out;
  wire [31:0] multiplexer_3_out, multiplexer_4_out;

  Multiplexer #(.Bits(3)) multiplexer_1 (.sel(rst), .in_0(id__alusel), .in_1(3'b000), .out(multiplexer_1_out));
  Multiplexer #(.Bits(8)) multiplexer_2 (.sel(rst), .in_0(id__aluop), .in_1({8{1'b0}}), .out(multiplexer_2_out));
  Multiplexer #(.Bits(32)) multiplexer_3 (.sel(rst), .in_0(id__reg1), .in_1({32{1'b0}}), .out(multiplexer_3_out));
  Multiplexer #(.Bits(32)) multiplexer_4 (.sel(rst), .in_0(id__reg2), .in_1({32{1'b0}}), .out(multiplexer_4_out));
  Multiplexer #(.Bits(5)) multiplexer_5 (.sel(rst), .in_0(id__wd), .in_1({5{1'b0}}), .out(multiplexer_5_out));
  Multiplexer multiplexer_6 (.sel(rst), .in_0(id__wreg), .in_1(1'b0), .out(multiplexer_6_out));
  Register #(.Bits(3)) register_1 (.D(multiplexer_1_out), .C(clk), .en(1'b1), .Q(ex__alusel));
  Register #(.Bits(8)) register_2 (.D(multiplexer_2_out), .C(clk), .en(1'b1), .Q(ex__aluop));
  Register #(.Bits(32)) register_3 (.D(multiplexer_3_out), .C(clk), .en(1'b1), .Q(ex__reg1));
  Register #(.Bits(32)) register_4 (.D(multiplexer_4_out), .C(clk), .en(1'b1), .Q(ex__reg2));
  Register #(.Bits(5)) register_5 (.D(multiplexer_5_out), .C(clk), .en(1'b1), .Q(ex__wd));
  Register register_6 (.D(multiplexer_6_out), .C(clk), .en(1'b1), .Q(ex__wreg));

  // Notes on the sheet:
  //   id__aluop: 譯碼階段的指令要進行的運算的子類型
  //   id__alusel: 譯碼階段的指令要進行的運算的類型
  //   id__reg1: 譯碼階段的指令要進行的運算的來源操作數1
  //   id__reg2: 譯碼階段的指令要進行的運算的來源操作數2
  //   id__wd: 譯碼階段的指令要寫入的目的暫存器位址
  //   id__wreg: 譯碼階段的指令是否有要寫入的目的暫存器
  //   rst: 復位信號
  //   ex__aluop: 執行階段的指令要進行的運算的子類型
  //   ex__alusel: 執行階段的指令要進行的運算的類型
  //   ex__reg1: 執行階段的指令要進行的運算的來源操作數1
  //   ex__reg2: 執行階段的指令要進行的運算的來源操作數
endmodule
