// Digital circuit if_id.dig as structural Verilog
module if_id (
  input  [31:0] if__pc,
  input  [31:0] if__inst,
  input  rst,
  input  clk,
  output [31:0] id__pc,
  output [31:0] id__inst
);

  wire [31:0] multiplexer_1_out, multiplexer_2_out;

  Multiplexer #(.Bits(32)) multiplexer_1 (.sel(rst), .in_0(if__inst), .in_1({32{1'b0}}), .out(multiplexer_1_out));
  Multiplexer #(.Bits(32)) multiplexer_2 (.sel(rst), .in_0(if__pc), .in_1({32{1'b0}}), .out(multiplexer_2_out));
  Register #(.Bits(32)) register_1 (.D(multiplexer_2_out), .C(clk), .en(1'b1), .Q(id__pc));
  Register #(.Bits(32)) register_2 (.D(multiplexer_1_out), .C(clk), .en(1'b1), .Q(id__inst));
endmodule
