// Digital circuit mem.dig as structural Verilog
module mem (
  input  [31:0] wdata__i,
  input  [4:0] wd__i,
  input  wreg__i,
  input  rst,
  output [31:0] wdata__o,
  output [4:0] wd__o,
  output wreg__o
);

  Multiplexer #(.Bits(5)) multiplexer_1 (.sel(rst), .in_0(wd__i), .in_1({5{1'b0}}), .out(wd__o));
  Multiplexer multiplexer_2 (.sel(rst), .in_0(wreg__i), .in_1(1'b0), .out(wreg__o));
  Multiplexer #(.Bits(32)) multiplexer_3 (.sel(rst), .in_0(wdata__i), .in_1({32{1'b0}}), .out(wdata__o));

  // Notes on the sheet:
  //   wdata__i: 訪存階段的指令要寫入目的暫存器的值
  //   wd__i: 訪存階段的指令要寫入的目的暫存器位址
  //   wreg__i: 訪存階段的指令是否有要寫入的目的暫存器
  //   rst: 復位信號
  //   wdata__o: 訪存階段的指令最終要寫入目的暫存器的值
  //   wd__o: 訪存階段的指令最終要寫入的目的暫存器位址
  //   wreg__o: 訪存階段的指令最終是否有要寫入的目的暫存器
endmodule
