// Digital circuit openmips.dig as structural Verilog
module openmips (
  input  rst,
  input  clk,
  input  [31:0] room__data__i,
  output rom__ce__o,
  output [31:0] room__addr__o
);

  wire ex_1_wreg__o, ex_mem_1_mem__wreg, id_1_reg1__read__o, id_1_reg2__read__o, id_1_wreg__o, id_ex_1_p14,
       mem_1_wreg__o, regfile_1_p7;
  wire [2:0] id_1_alusel__o, id_ex_1_p10;
  wire [4:0] ex_1_wd__o, ex_mem_1_mem__wd, id_1_reg1__addr__o, id_1_reg2__addr__o, id_1_wd__o, id_ex_1_p13,
       mem_1_wd__o, regfile_1_p8;
  wire [7:0] id_1_aluop__o, id_ex_1_p9;
  wire [31:0] ex_1_wdata__o, ex_mem_1_mem__wdata, id_1_reg1__o, id_1_reg2__o, id_ex_1_p11, id_ex_1_p12,
       if_id_1_id__inst, if_id_1_id__pc, mem_1_wdata__o, regfile_1_p1, regfile_1_p2, regfile_1_p9;

  pc_reg pc_reg_1 (.rst(rst), .clk(clk), .pc(room__addr__o), .ce(rom__ce__o));
  if_id if_id_1 (
    .if__pc(room__addr__o), .if__inst(room__data__i), .rst(rst), .clk(clk), .id__pc(if_id_1_id__pc),
    .id__inst(if_id_1_id__inst));
  id id_1 (
    .pc__i(if_id_1_id__pc), .inst__i(if_id_1_id__inst), .reg1__data__i(regfile_1_p2),
    .reg2__data__i(regfile_1_p1), .rst(rst), .aluop__o(id_1_aluop__o), .alusel__o(id_1_alusel__o),
    .reg1__o(id_1_reg1__o), .reg2__o(id_1_reg2__o), .wd__o(id_1_wd__o), .wreg__o(id_1_wreg__o),
    .reg2__addr__o(id_1_reg2__addr__o), .reg2__read__o(id_1_reg2__read__o),
    .reg1__addr__o(id_1_reg1__addr__o), .reg1__read__o(id_1_reg1__read__o));
  // regfile regfile_1: pin names not known; wires that end beside it: regfile_1_p1, regfile_1_p2, id_1_reg1__read__o, id_1_reg1__addr__o, id_1_reg2__read__o, id_1_reg2__addr__o, regfile_1_p7, regfile_1_p8, regfile_1_p9, rst, clk
  // id_ex id_ex_1: pin names not known; wires that end beside it: id_1_aluop__o, id_1_alusel__o, id_1_reg1__o, id_1_reg2__o, id_1_wd__o, id_1_wreg__o, rst, clk, id_ex_1_p9, id_ex_1_p10, id_ex_1_p11, id_ex_1_p12, id_ex_1_p13, id_ex_1_p14
  ex ex_1 (
    .aluop__i(id_ex_1_p9), .alusel__i(id_ex_1_p10), .reg1__i(id_ex_1_p11), .reg2__i(id_ex_1_p12),
    .wd__i(id_ex_1_p13), .wreg__i(id_ex_1_p14), .rst(rst), .wdata__o(ex_1_wdata__o), .wd__o(ex_1_wd__o),
    .wreg__o(ex_1_wreg__o));
  ex_mem ex_mem_1 (
    .ex__wdata(ex_1_wdata__o), .ex__wd(ex_1_wd__o), .ex__wreg(ex_1_wreg__o), .rst(rst), .clk(clk),
    .mem__wdata(ex_mem_1_mem__wdata), .mem__wd(ex_mem_1_mem__wd), .mem__wreg(ex_mem_1_mem__wreg));
  mem mem_1 (
    .wdata__i(ex_mem_1_mem__wdata), .wd__i(ex_mem_1_mem__wd), .wreg__i(ex_mem_1_mem__wreg), .rst(rst),
    .wdata__o(mem_1_wdata__o), .wd__o(mem_1_wd__o), .wreg__o(mem_1_wreg__o));
  mem_wb mem_wb_1 (
    .mem__wdata(mem_1_wdata__o), .mem__wd(mem_1_wd__o), .mem__wreg(mem_1_wreg__o), .rst(rst), .clk(clk),
    .wb__wdata(regfile_1_p9), .wb__wd(regfile_1_p8), .wb__wreg(regfile_1_p7));
endmodule
