// Digital circuit pc_reg.dig as structural Verilog
module pc_reg (
  input  rst,
  input  clk,
  output [31:0] pc,
  output ce
);

  CounterPreset #(.Bits(32)) counterpreset_1 (
    .en(1'b1), .C(clk), .dir(1'b0), .in({32{1'b0}}), .ld(1'b0), .clr(rst), .out(pc));  // open: ovf
  not not_1 (ce, rst);
endmodule
