// Digital circuit reg_32.dig as structural Verilog
module reg_32 (
  input  clk,
  input  we,
  input  [4:0] waddr,
  input  [31:0] wdata,
  input  re1,
  input  [4:0] raddr1,
  input  re2,
  input  [4:0] raddr2,
  output [31:0] A_1,
  output [31:0] A_2
);

  wire [31:0] multiplexer_1_out, multiplexer_2_out, Q_0, Q_1, Q_2, Q_3, Q_4, Q_5, Q_6, Q_7, Q_8, Q_9, Q_10,
       Q_11, Q_12, Q_13, Q_14, Q_15, Q_16, Q_17, Q_18, Q_19, Q_20, Q_21, Q_22, Q_23, Q_24, Q_25, Q_26, Q_27,
       Q_28, Q_29, Q_30, Q_31, reg_0, reg_1, reg_2, reg_3, reg_4, reg_5, reg_6, reg_7, reg_8, reg_9, reg_10,
       reg_11, reg_12, reg_13, reg_14, reg_15, reg_16, reg_17, reg_18, reg_19, reg_20, reg_21, reg_22,
       reg_23, reg_24, reg_25, reg_26, reg_27, reg_28, reg_29, reg_30, reg_31;

  Demultiplexer #(.Selector_Bits(5), .Bits(32)) demultiplexer_1 (
    .sel(waddr), .in(wdata), .out_0(reg_0), .out_1(reg_1), .out_2(reg_2), .out_3(reg_3), .out_4(reg_4),
    .out_5(reg_5), .out_6(reg_6), .out_7(reg_7), .out_8(reg_8), .out_9(reg_9), .out_10(reg_10),
    .out_11(reg_11), .out_12(reg_12), .out_13(reg_13), .out_14(reg_14), .out_15(reg_15), .out_16(reg_16),
    .out_17(reg_17), .out_18(reg_18), .out_19(reg_19), .out_20(reg_20), .out_21(reg_21), .out_22(reg_22),
    .out_23(reg_23), .out_24(reg_24), .out_25(reg_25), .out_26(reg_26), .out_27(reg_27), .out_28(reg_28),
    .out_29(reg_29), .out_30(reg_30), .out_31(reg_31));
  Register #(.Bits(32)) register_1 (.D(reg_0), .C(clk), .en(we), .Q(Q_0));
  Register #(.Bits(32)) register_2 (.D(reg_4), .C(clk), .en(we), .Q(Q_4));
  Register #(.Bits(32)) register_3 (.D(reg_8), .C(clk), .en(we), .Q(Q_8));
  Register #(.Bits(32)) register_4 (.D(reg_12), .C(clk), .en(we), .Q(Q_12));
  Register #(.Bits(32)) register_5 (.D(reg_16), .C(clk), .en(we), .Q(Q_16));
  Register #(.Bits(32)) register_6 (.D(reg_20), .C(clk), .en(we), .Q(Q_20));
  Register #(.Bits(32)) register_7 (.D(reg_24), .C(clk), .en(we), .Q(Q_24));
  Register #(.Bits(32)) register_8 (.D(reg_28), .C(clk), .en(we), .Q(Q_28));
  Register #(.Bits(32)) register_9 (.D(reg_1), .C(clk), .en(we), .Q(Q_1));
  Register #(.Bits(32)) register_10 (.D(reg_5), .C(clk), .en(we), .Q(Q_5));
  Register #(.Bits(32)) register_11 (.D(reg_9), .C(clk), .en(we), .Q(Q_9));
  Register #(.Bits(32)) register_12 (.D(reg_13), .C(clk), .en(we), .Q(Q_13));
  Register #(.Bits(32)) register_13 (.D(reg_17), .C(clk), .en(we), .Q(Q_17));
  Register #(.Bits(32)) register_14 (.D(reg_21), .C(clk), .en(we), .Q(Q_21));
  Register #(.Bits(32)) register_15 (.D(reg_25), .C(clk), .en(we), .Q(Q_25));
  Register #(.Bits(32)) register_16 (.D(reg_29), .C(clk), .en(we), .Q(Q_29));
  Register #(.Bits(32)) register_17 (.D(reg_2), .C(clk), .en(we), .Q(Q_2));
  Register #(.Bits(32)) register_18 (.D(reg_6), .C(clk), .en(we), .Q(Q_6));
  Register #(.Bits(32)) register_19 (.D(reg_10), .C(clk), .en(we), .Q(Q_10));
  Register #(.Bits(32)) register_20 (.D(reg_14), .C(clk), .en(we), .Q(Q_14));
  Register #(.Bits(32)) register_21 (.D(reg_18), .C(clk), .en(we), .Q(Q_18));
  Register #(.Bits(32)) register_22 (.D(reg_22), .C(clk), .en(we), .Q(Q_22));
  Register #(.Bits(32)) register_23 (.D(reg_26), .C(clk), .en(we), .Q(Q_26));
  Register #(.Bits(32)) register_24 (.D(reg_30), .C(clk), .en(we), .Q(Q_30));
  Register #(.Bits(32)) register_25 (.D(reg_3), .C(clk), .en(we), .Q(Q_3));
  Register #(.Bits(32)) register_26 (.D(reg_7), .C(clk), .en(we), .Q(Q_7));
  Register #(.Bits(32)) register_27 (.D(reg_11), .C(clk), .en(we), .Q(Q_11));
  Register #(.Bits(32)) register_28 (.D(reg_15), .C(clk), .en(we), .Q(Q_15));
  Register #(.Bits(32)) register_29 (.D(reg_19), .C(clk), .en(we), .Q(Q_19));
  Register #(.Bits(32)) register_30 (.D(reg_23), .C(clk), .en(we), .Q(Q_23));
  Register #(.Bits(32)) register_31 (.D(reg_27), .C(clk), .en(we), .Q(Q_27));
  Register #(.Bits(32)) register_32 (.D(reg_31), .C(clk), .en(we), .Q(Q_31));
  Multiplexer #(.Selector_Bits(5), .Bits(32)) multiplexer_1 (
    .sel(raddr1), .in_0(Q_0), .in_1(Q_1), .in_2(Q_2), .in_3(Q_3), .in_4(Q_4), .in_5(Q_5), .in_6(Q_6),
    .in_7(Q_7), .in_8(Q_8), .in_9(Q_9), .in_10(Q_10), .in_11(Q_11), .in_12(Q_12), .in_13(Q_13), .in_14(Q_14),
    .in_15(Q_15), .in_16(Q_16), .in_17(Q_17), .in_18(Q_18), .in_19(Q_19), .in_20(Q_20), .in_21(Q_21),
    .in_22(Q_22), .in_23(Q_23), .in_24(Q_24), .in_25(Q_25), .in_26(Q_26), .in_27(Q_27), .in_28(Q_28),
    .in_29(Q_29), .in_30(Q_30), .in_31(Q_31), .out(multiplexer_1_out));
  Multiplexer #(.Selector_Bits(5), .Bits(32)) multiplexer_2 (
    .sel(raddr2), .in_0(Q_0), .in_1(Q_1), .in_2(Q_2), .in_3(Q_3), .in_4(Q_4), .in_5(Q_5), .in_6(Q_6),
    .in_7(Q_7), .in_8(Q_8), .in_9(Q_9), .in_10(Q_10), .in_11(Q_11), .in_12(Q_12), .in_13(Q_13), .in_14(Q_14),
    .in_15(Q_15), .in_16(Q_16), .in_17(Q_17), .in_18(Q_18), .in_19(Q_19), .in_20(Q_20), .in_21(Q_21),
    .in_22(Q_22), .in_23(Q_23), .in_24(Q_24), .in_25(Q_25), .in_26(Q_26), .in_27(Q_27), .in_28(Q_28),
    .in_29(Q_29), .in_30(Q_30), .in_31(Q_31), .out(multiplexer_2_out));
  Multiplexer #(.Bits(32)) multiplexer_3 (.sel(re1), .in_0({32{1'b0}}), .in_1(multiplexer_1_out), .out(A_1));
  Multiplexer #(.Bits(32)) multiplexer_4 (.sel(re2), .in_0({32{1'b0}}), .in_1(multiplexer_2_out), .out(A_2));

  // Other names for the same wires on the sheet: raddr_1[4:0] = raddr1; raddr_2[4:0] = raddr2; re_1 = re1; re_2 = re2

  // Notes on the sheet:
  //   A_1: 第一個讀取暫存器連接埠輸出的暫存器值
  //   A_2: 第二個讀取暫存器連接埠輸出的暫存器值
endmodule
